// Logisim project universal_shift_register.circ as structural Verilog: 1 circuit, main circuit main
module main (
  input  [3:0] in_1,
  input  in_2,
  input  [1:0] in_3,
  output [3:0] out_4
);

  wire clock_1_out, multiplexer_1_out, multiplexer_2_out, multiplexer_3_out, multiplexer_4_out;

  Multiplexer #(.select(2)) multiplexer_1 (
    .in0(in_2), .in1(in_1[0]), .in2(out_4[1]), .in3(out_4[0]), .out(multiplexer_1_out), .sel(in_3));
  D_Flip_Flop d_ff_1 (.D(multiplexer_1_out), .clk(clock_1_out), .Q(out_4[0]));  // open: Qn, preset, reset
  Clock clock_1 (.out(clock_1_out));
  Multiplexer #(.select(2)) multiplexer_2 (
    .in0(out_4[0]), .in1(in_1[1]), .in2(out_4[2]), .in3(out_4[1]), .out(multiplexer_2_out), .sel(in_3));
  D_Flip_Flop d_ff_2 (.D(multiplexer_2_out), .clk(clock_1_out), .Q(out_4[1]));  // open: Qn, preset, reset
  Multiplexer #(.select(2)) multiplexer_3 (
    .in0(out_4[1]), .in1(in_1[2]), .in2(out_4[3]), .in3(out_4[2]), .out(multiplexer_3_out), .sel(in_3));
  D_Flip_Flop d_ff_3 (.D(multiplexer_3_out), .clk(clock_1_out), .Q(out_4[2]));  // open: Qn, preset, reset
  Multiplexer #(.select(2)) multiplexer_4 (
    .in0(out_4[2]), .in1(in_1[3]), .in2(in_2), .in3(out_4[3]), .out(multiplexer_4_out), .sel(in_3));
  D_Flip_Flop d_ff_4 (.D(multiplexer_4_out), .clk(clock_1_out), .Q(out_4[3]));  // open: Qn, preset, reset
endmodule
